// Logisim project COMPUTER_Four.circ as structural Verilog: 8 circuits, main circuit main
module main (
);

  wire AccumulatorEquals, AccuOut, ACUEQU, AL, and_1_out, and_4_out, and_5_out, and_6_out, and_10_out,
       and_11_out, Borrow, Carry, CB, Clk, clock_1_out, CNTOVER, CNTOVERFLOW, comparator_1_eq,
       comparator_2_eq, COUT, DATEQU, decoder_1_out0, Dev, FLAG, GP1, GP2, Halt, IsBorrow, IsCarry, IsZero,
       JMPACUEQU, JMPCB, JMPCNTOVER, JMPDATA, JMPDATEQU, JMPZERO, JUMP, MISC, multiplexer_1_out, not_1_out,
       not_2_out, not_3_out, not_4_out, or_1_out, or_3_out, Ou, OUTF0, OutputEnable, PCLoad, PCtoDAT, POWER,
       PrgOrMem, RAMact, ReadLN, RESET, ResetCOUT, ROMact, RomToData, SAVE, SetA, SetCount, SetEqualREG,
       START, STOP, Wr, WriteEnable, WriteOut, Zero;
  wire [10:0] Add;
  wire [11:0] Data, GPInput, GPO1, GPO2, InstData, Out0, PCIn, ProgramCount, ReadIn;
  wire [15:0] DataBUS, rom_1_data;
  wire [15:12] controlled_buffer_2_out, Instructions;
  wire [23:0] His;

  and and_1 (and_1_out, POWER, not_1_out, not_2_out);
  Multiplexer #(.enable("false")) multiplexer_1 (.in0(Carry), .in1(Borrow), .out(multiplexer_1_out), .sel(CB));
  or or_1 (or_1_out, START, STOP);
  not not_1 (not_1_out, Halt);
  not not_2 (not_2_out, PrgOrMem);
  Register #(.width(16)) register_1 (.D(DataBUS), .en(not_3_out), .clk(Clk), .Q({Instructions, InstData}), .clr(RESET));
  not not_3 (not_3_out, PrgOrMem);
  // Shift_Register #(.width(12), .length(2)) shift_register_1: pin names not known; wires that end beside it: RESET, 1'b0, OUTF0, Clk, Out0, His[23:12]
  Counter #(.width(12), .max('hfff), .ongoal("stay")) counter_1 (
    .clr(or_1_out), .load(PCLoad), .up(1'b1), .count(and_1_out), .clk(Clk), .D(PCIn), .Q(ProgramCount));  // open: carry
  JMP jmp_1 (
    .JMP(JUMP), .JMPZERO(JMPZERO), .ZERO(Zero), .JMPCARRYBORROW(JMPCB), .CARRYBORROW(multiplexer_1_out),
    .JMPDATA(JMPDATA), .JMPACUEQU(JMPACUEQU), .ACUEQU(ACUEQU), .JMPDATEQU(JMPDATEQU), .DATEQU(DATEQU),
    .JMPCNTOVER(JMPCNTOVER), .CNTOVER(CNTOVER), .ROM(InstData), .DATA(Data), .PCLoad(PCLoad), .PCIn(PCIn));
  Register #(.width(12)) register_2 (.D(Data), .en(OUTF0), .clk(Clk), .Q(Out0), .clr(RESET));
  Register #(.width(12)) register_3 (.D(Data), .en(GP1), .clk(Clk), .Q(GPO1), .clr(RESET));
  Register #(.width(12)) register_4 (.D(Data), .en(GP2), .clk(Clk), .Q(GPO2), .clr(RESET));
  FLG flg_1 (
    .FLG(FLAG), .ROM(InstData), .IsCarry(IsCarry), .IsZero(IsZero), .AccumulatorEquals(AccumulatorEquals),
    .CNTOverflow(CNTOVERFLOW), .Borrow(IsBorrow), .START(START), .STOP(STOP), .Clock(Clk), .WriteOut(OUTF0),
    .PCtoDAT(PCtoDAT), .AccuOut(AccuOut), .RomToData(RomToData), .Carry(Carry), .Zero(Zero), .AcuEqu(ACUEQU),
    .CorB(CB), .CNTOverFlag(CNTOVER), .BorrowFlag(Borrow), .Power(POWER));
  ALU alu_1 (
    .ALU(AL), .DATAIn(Data), .SetA(SetA), .AccumulatorOut(AccuOut), .ROM(InstData),
    .SetEqualREG(SetEqualREG), .Clock(Clk), .DATAOut(Data), .AccumulatorIsZero(IsZero), .CarryOut(IsCarry),
    .BorrowOut(IsBorrow), .DataEquals(DATEQU), .AccumulatorEquals(AccumulatorEquals));
  Decoder #(.enable("false")) decoder_1 (.out0(decoder_1_out0), .out1(RAMact), .sel(Dev));
  and and_2 (ROMact, Ou, decoder_1_out0);
  Comparator #(.width(12)) comparator_1 (.a(InstData), .b(12'hffe), .eq(comparator_1_eq));  // open: gt, lt
  Comparator #(.width(12)) comparator_2 (.a(InstData), .b({12{1'b1}}), .eq(comparator_2_eq));  // open: gt, lt
  Multiplexer #(.width(12), .enable("false")) multiplexer_2 (
    .in0(ProgramCount), .in1(InstData), .out({Dev, Add}), .sel(WriteEnable));
  and and_3 (Wr, WriteEnable, PrgOrMem);
  not not_4 (not_4_out, PrgOrMem);
  or or_2 (Ou, not_4_out, and_4_out);
  and and_4 (and_4_out, PrgOrMem, OutputEnable);
  Decoder #(.select(4)) decoder_2 (
    .out1(FLAG), .out2(JUMP), .out3(JMPDATA), .out4(JMPZERO), .out5(JMPCB), .out6(JMPACUEQU),
    .out7(JMPDATEQU), .out8(JMPCNTOVER), .out9(AL), .out10(SetA), .out11(SetEqualREG), .out12(SetCount),
    .out13(COUT), .out14(SAVE), .out15(MISC), .sel(Instructions), .en(PrgOrMem));  // open: out0
  and and_5 (and_5_out, WriteEnable, PrgOrMem);
  and and_6 (and_6_out, PrgOrMem, OutputEnable);
  and and_7 (GP1, comparator_1_eq, WriteEnable);
  and and_8 (GP2, comparator_2_eq, WriteEnable);
  T_Flip_Flop t_ff_1 (.T(1'b1), .clk(Clk), .Q(PrgOrMem));  // open: Qn, reset, preset
  Clock clock_1 (.out(clock_1_out));
  or or_3 (or_3_out, Halt, ~POWER);  // OR_Gate
  or or_4 (RESET, START, STOP);
  Pull_Resistor pull_resistor_1 (.node(DataBUS));
  and and_9 (Clk, clock_1_out, ~or_3_out);  // AND_Gate
  assign DataBUS = and_5_out ? {controlled_buffer_2_out, Data} : 16'bz;  // Controlled_Buffer controlled_buffer_1
  Pull_Resistor pull_resistor_2 (.node(Data));
  assign {controlled_buffer_2_out, Data} = and_6_out ? DataBUS : 16'bz;  // Controlled_Buffer controlled_buffer_2
  assign Data = RomToData ? InstData : 12'bz;  // Controlled_Buffer controlled_buffer_3
  assign Data = PCtoDAT ? ProgramCount : 12'bz;  // Controlled_Buffer controlled_buffer_4
  RAM #(.addrWidth(11), .dataWidth(16)) ram_1 (.addr(Add), .we(and_10_out), .oe(and_11_out), .clk(Clk), .data(DataBUS));
  and and_10 (and_10_out, Wr, RAMact);
  and and_11 (and_11_out, RAMact, Ou);
  ROM #(.addrWidth(11), .dataWidth(16)) rom_1 (.addr(Add), .data(rom_1_data));
  Stack stack_1 (.Misc(MISC), .ROM(InstData), .Data(Data), .Clock(Clk), .ReadStack(Data), .ResetCOUT(ResetCOUT));
  Save_Load save_load_1 (
    .WriteEnable(WriteEnable), .ROM(InstData), .Clk(Clk), .OutputEnable(OutputEnable), .SAVE(SAVE),
    .MISC(MISC));
  ReadCirc readcirc_1 (
    .MISC(MISC), .ROM(InstData), .ReadIn(ReadIn), .Button(ReadLN), .Clk(Clk), .GPInput(GPInput),
    .START(START), .STOP(STOP), .DATA(Data), .HALT(Halt));
  Count count_1 (
    .MISC(MISC), .ROM(InstData), .DATA(Data), .SetCount(SetCount), .Clock(Clk), .CNTOUT(Data),
    .CNTOverflow(CNTOVERFLOW));
  assign DataBUS = ROMact ? rom_1_data : 16'bz;  // Controlled_Buffer controlled_buffer_5
  Button button_1 (.out(ReadLN));
  DipSwitch #(.number(12)) dipswitch_1 (
    .sw1(ReadIn[11]), .sw2(ReadIn[10]), .sw3(ReadIn[9]), .sw4(ReadIn[8]), .sw5(ReadIn[7]), .sw6(ReadIn[6]),
    .sw7(ReadIn[5]), .sw8(ReadIn[4]), .sw9(ReadIn[3]), .sw10(ReadIn[2]), .sw11(ReadIn[1]), .sw12(ReadIn[0]));
  DipSwitch #(.number(12)) dipswitch_2 (
    .sw1(GPInput[11]), .sw2(GPInput[10]), .sw3(GPInput[9]), .sw4(GPInput[8]), .sw5(GPInput[7]),
    .sw6(GPInput[6]), .sw7(GPInput[5]), .sw8(GPInput[4]), .sw9(GPInput[3]), .sw10(GPInput[2]),
    .sw11(GPInput[1]), .sw12(GPInput[0]));
  Button button_2 (.out(START));
  // BCD_to_7_Segment_decoder bcd_to_7_segment_decoder_1: pin names not known
  _7_Segment_Display u_7_segment_display_1 ();  // open: g, f, a, b, e, d, c, dp
  // BCD_to_7_Segment_decoder bcd_to_7_segment_decoder_2: pin names not known
  _7_Segment_Display u_7_segment_display_2 ();  // open: g, f, a, b, e, d, c, dp
  // Binairy_to_BCD_converter #(.binvalue(12)) binairy_to_bcd_converter_1: pin names not known; wires that end beside it: Out0
  _7_Segment_Display u_7_segment_display_3 ();  // open: g, f, a, b, e, d, c, dp
  _7_Segment_Display u_7_segment_display_4 ();  // open: g, f, a, b, e, d, c, dp
  // BCD_to_7_Segment_decoder bcd_to_7_segment_decoder_3: pin names not known
  // BCD_to_7_Segment_decoder bcd_to_7_segment_decoder_4: pin names not known
  // Binairy_to_BCD_converter #(.binvalue(12)) binairy_to_bcd_converter_2: pin names not known; wires that end beside it: ReadIn
  Button button_3 (.out(STOP));
  _7_Segment_Display u_7_segment_display_5 ();  // open: g, f, a, b, e, d, c, dp
  // BCD_to_7_Segment_decoder bcd_to_7_segment_decoder_5: pin names not known
  // BCD_to_7_Segment_decoder bcd_to_7_segment_decoder_6: pin names not known
  _7_Segment_Display u_7_segment_display_6 ();  // open: g, f, a, b, e, d, c, dp
  Hex_Digit_Display hex_digit_display_1 (.value(ProgramCount[7:4]), .dp(ProgramCount[0]));
  // Hex_Digit_Display hex_digit_display_2: pin names not known; wires that end beside it: ProgramCount[11:8]
  DotMatrix #(.inputtype("row"), .matrixcols(12), .matrixrows(1)) dotmatrix_1 (.row0(His[11:0]));
  DotMatrix #(.inputtype("row"), .matrixcols(12), .matrixrows(1)) dotmatrix_2 (.row0(His[23:12]));
  DotMatrix #(.inputtype("row"), .matrixcols(12), .matrixrows(1)) dotmatrix_3 (.row0(GPO1));
  DotMatrix #(.inputtype("row"), .matrixcols(12), .matrixrows(1)) dotmatrix_4 (.row0(GPO2));
  TTY #(.rows(4), .cols(20)) tty_1 (.data(Data[6:0]), .clk(Clk), .we(COUT), .clr(ResetCOUT));
  _7_Segment_Display u_7_segment_display_7 ();  // open: g, f, a, b, e, d, c, dp
  // BCD_to_7_Segment_decoder bcd_to_7_segment_decoder_7: pin names not known
  // BCD_to_7_Segment_decoder bcd_to_7_segment_decoder_8: pin names not known
  _7_Segment_Display u_7_segment_display_8 ();  // open: g, f, a, b, e, d, c, dp
  Hex_Digit_Display hex_digit_display_3 (.value(ProgramCount[3:0]));  // open: dp
  LED led_1 (.in(WriteOut));
  LED led_2 (.in(Carry));
  LED led_3 (.in(Borrow));
  LED led_4 (.in(Zero));
  // Hex_Digit_Display hex_digit_display_4: pin names not known; wires that end beside it: InstData[11:8]
  Hex_Digit_Display hex_digit_display_5 (.value(Instructions));  // open: dp
  LED led_5 (.in(AccuOut));
  LED led_6 (.in(DATEQU));
  LED led_7 (.in(CB));
  LED led_8 (.in(CNTOVER));
  LED led_9 (.in(Halt));
  LED led_10 (.in(POWER));
  Hex_Digit_Display hex_digit_display_6 (.value(InstData[7:4]), .dp(InstData[0]));
  Hex_Digit_Display hex_digit_display_7 (.value(InstData[3:0]));  // open: dp
  LED led_11 (.in(RomToData));
  LED led_12 (.in(ACUEQU));
  LED led_13 (.in(PCtoDAT));
  Hex_Digit_Display hex_digit_display_8 (.value(Data[7:4]), .dp(Data[0]));
  // Hex_Digit_Display hex_digit_display_9: pin names not known; wires that end beside it: Data[11:8]
  Hex_Digit_Display hex_digit_display_10 (.value(Data[3:0]));  // open: dp
  // Pins of 1 and 4 bits meet at ProgramCount[3:0]
  // Pins of 1 and 4 bits meet at InstData[3:0]
  // Pins of 1 and 4 bits meet at Data[3:0]

  // Other names for the same wires on the sheet: Instructions[11:0] = InstData

  // Notes on the sheet:
  //   contents of rom_1 (hex, n*v repeats v):
  //   f800 f700 a000 f700 b000 f900 f300 700b 9000 f000 2007 f400 1300 efff 1000 1000 1000 1e00 1f00
endmodule

module JMP (
  input  JMP,
  input  JMPZERO,
  input  ZERO,
  input  JMPCARRYBORROW,
  input  CARRYBORROW,
  input  JMPDATA,
  input  JMPACUEQU,
  input  ACUEQU,
  input  JMPDATEQU,
  input  DATEQU,
  input  JMPCNTOVER,
  input  CNTOVER,
  input  [11:0] ROM,
  input  [11:0] DATA,
  output PCLoad,
  output [11:0] PCIn
);

  wire and_1_out, and_2_out, and_3_out, and_4_out, and_5_out;

  and and_1 (and_1_out, JMPZERO, ZERO);
  and and_2 (and_2_out, JMPCARRYBORROW, CARRYBORROW);
  and and_3 (and_3_out, JMPACUEQU, ACUEQU);
  and and_4 (and_4_out, JMPDATEQU, DATEQU);
  and and_5 (and_5_out, JMPCNTOVER, CNTOVER);
  or or_1 (PCLoad, JMP, and_1_out, and_2_out, JMPDATA, and_3_out, and_4_out, and_5_out);
  Multiplexer #(.width(12), .enable("false")) multiplexer_1 (.in0(ROM), .in1(DATA), .out(PCIn), .sel(JMPDATA));
endmodule

module FLG (
  input  FLG,
  input  [11:0] ROM,
  input  IsCarry,
  input  IsZero,
  input  AccumulatorEquals,
  input  CNTOverflow,
  input  Borrow,
  input  START,
  input  STOP,
  input  Clock,
  output WriteOut,
  output PCtoDAT,
  output AccuOut,
  output RomToData,
  output Carry,
  output Zero,
  output AcuEqu,
  output CorB,
  output CNTOverFlag,
  output BorrowFlag,
  output Power
);

  wire decoder_1_out1, decoder_1_out2, decoder_1_out3, decoder_1_out4, decoder_1_out5, decoder_1_out6,
       decoder_1_out7, decoder_1_out8, decoder_1_out9, decoder_1_out10, decoder_1_out11, decoder_1_out12,
       decoder_1_out13, decoder_1_out14, decoder_1_out15, or_1_out, or_2_out;

  Decoder #(.select(4)) decoder_1 (
    .out0(WriteOut), .out1(decoder_1_out1), .out2(decoder_1_out2), .out3(decoder_1_out3),
    .out4(decoder_1_out4), .out5(decoder_1_out5), .out6(decoder_1_out6), .out7(decoder_1_out7),
    .out8(decoder_1_out8), .out9(decoder_1_out9), .out10(decoder_1_out10), .out11(decoder_1_out11),
    .out12(decoder_1_out12), .out13(decoder_1_out13), .out14(decoder_1_out14), .out15(decoder_1_out15),
    .sel(ROM[11:8]), .en(FLG));
  or or_1 (or_1_out, STOP, START, decoder_1_out14);
  or or_2 (or_2_out, decoder_1_out15, STOP);
  S_R_Flip_Flop s_r_ff_1 (
    .S(decoder_1_out1), .R(decoder_1_out2), .clk(Clock), .Q(PCtoDAT), .reset(or_1_out));  // open: Qn, preset
  S_R_Flip_Flop AccuOutf (
    .S(decoder_1_out3), .R(decoder_1_out4), .clk(Clock), .Q(AccuOut), .reset(or_1_out));  // open: Qn, preset
  S_R_Flip_Flop RomToDataf (
    .S(decoder_1_out5), .R(decoder_1_out6), .clk(Clock), .Q(RomToData), .reset(or_1_out));  // open: Qn, preset
  S_R_Flip_Flop Carryf (.S(IsCarry), .R(decoder_1_out7), .clk(Clock), .Q(Carry), .reset(or_1_out));  // open: Qn, preset
  S_R_Flip_Flop Zerof (.S(IsZero), .R(decoder_1_out8), .clk(Clock), .Q(Zero), .reset(or_1_out));  // open: Qn, preset
  S_R_Flip_Flop AccumEqualsf (
    .S(AccumulatorEquals), .R(decoder_1_out9), .clk(Clock), .Q(AcuEqu), .reset(or_1_out));  // open: Qn, preset
  S_R_Flip_Flop s_r_ff_2 (
    .S(decoder_1_out12), .R(decoder_1_out13), .clk(Clock), .Q(CorB), .reset(or_1_out));  // open: Qn, preset
  S_R_Flip_Flop CNTOVERf (
    .S(CNTOverflow), .R(decoder_1_out10), .clk(Clock), .Q(CNTOverFlag), .reset(or_1_out));  // open: Qn, preset
  S_R_Flip_Flop Borrowf (
    .S(Borrow), .R(decoder_1_out11), .clk(Clock), .Q(BorrowFlag), .reset(or_1_out));  // open: Qn, preset
  S_R_Flip_Flop Powerf (.S(1'b0), .R(or_2_out), .clk(Clock), .Q(Power), .preset(START));  // open: reset, Qn
endmodule

module ALU (
  input  ALU,
  input  [11:0] DATAIn,
  input  SetA,
  input  AccumulatorOut,
  input  [11:0] ROM,
  input  SetEqualREG,
  input  Clock,
  output [11:0] DATAOut,
  output AccumulatorIsZero,
  output CarryOut,
  output BorrowOut,
  output DataEquals,
  output AccumulatorEquals
);

  wire and_1_out, and_2_out, BorrowIn_q, CarryIn_q, decoder_1_out0, decoder_1_out1, decoder_1_out2,
       decoder_1_out3, decoder_1_out4, decoder_1_out5, decoder_1_out6, decoder_1_out7, or_1_out, or_2_out;
  wire [11:0] A_q, Accumulator_q, adder_1_out, controlled_buffer_1_out, nand_1_out, register_1_q,
       subtractor_1_out;

  Decoder #(.select(3)) decoder_1 (
    .out0(decoder_1_out0), .out1(decoder_1_out1), .out2(decoder_1_out2), .out3(decoder_1_out3),
    .out4(decoder_1_out4), .out5(decoder_1_out5), .out6(decoder_1_out6), .out7(decoder_1_out7),
    .sel(ROM[10:8]), .en(ALU));
  Register #(.width(12)) A (.D(DATAIn), .en(SetA), .clk(Clock), .Q(A_q));  // open: clr
  Register #(.width(12)) register_1 (.D(DATAIn), .en(SetEqualREG), .clk(Clock), .Q(register_1_q));  // open: clr
  S_R_Flip_Flop BorrowIn (
    .S(decoder_1_out6), .R(decoder_1_out7), .clk(Clock), .Q(BorrowIn_q));  // open: reset, Qn, preset
  S_R_Flip_Flop CarryIn (
    .S(decoder_1_out4), .R(decoder_1_out5), .clk(Clock), .Q(CarryIn_q));  // open: reset, Qn, preset
  and and_1 (and_1_out, decoder_1_out3, ALU);
  Comparator #(.width(12)) comparator_1 (.a(DATAIn), .b(register_1_q), .eq(DataEquals));  // open: gt, lt
  Adder #(.width(12)) adder_1 (.a(Accumulator_q), .b(A_q), .out(adder_1_out), .cin(CarryIn_q), .cout(CarryOut));
  assign nand_1_out = ~(Accumulator_q & A_q);  // NAND_Gate nand_1, 12 bits wide
  or or_1 (or_1_out, decoder_1_out0, decoder_1_out1, decoder_1_out2);
  Subtractor #(.width(12)) subtractor_1 (
    .a(Accumulator_q), .b(A_q), .out(subtractor_1_out), .bin(BorrowIn_q), .bout(BorrowOut));
  assign controlled_buffer_1_out = decoder_1_out1 ? subtractor_1_out : 12'bz;  // Controlled_Buffer controlled_buffer_1
  assign controlled_buffer_1_out = decoder_1_out0 ? adder_1_out : 12'bz;  // Controlled_Buffer controlled_buffer_2
  assign controlled_buffer_1_out = decoder_1_out2 ? nand_1_out : 12'bz;  // Controlled_Buffer controlled_buffer_3
  and and_2 (and_2_out, or_1_out, ALU);
  Pull_Resistor pull_resistor_1 (.node(controlled_buffer_1_out));
  Register #(.width(12)) Accumulator (
    .D(controlled_buffer_1_out), .en(and_2_out), .clk(Clock), .Q(Accumulator_q), .clr(and_1_out));
  assign DATAOut = AccumulatorOut ? Accumulator_q : 12'bz;  // Controlled_Buffer controlled_buffer_4
  Comparator #(.width(12)) comparator_2 (.a(Accumulator_q), .b(register_1_q), .eq(AccumulatorEquals));  // open: gt, lt
  or or_2 (or_2_out, Accumulator_q[5], Accumulator_q[0], Accumulator_q[1], Accumulator_q[2], Accumulator_q[3], Accumulator_q[4], Accumulator_q[6], Accumulator_q[7], Accumulator_q[8], Accumulator_q[9], Accumulator_q[10], Accumulator_q[11]);
  not not_1 (AccumulatorIsZero, or_2_out);
endmodule

module Stack (
  input  Misc,
  input  [11:0] ROM,
  input  [11:0] Data,
  input  Clock,
  output [11:0] ReadStack,
  output ResetCOUT
);

  wire and_1_out, and_2_out, decoder_1_out10, decoder_1_out11, decoder_1_out12, decoder_1_out13, s_r_ff_1_q;
  wire [11:0] shift_register_1_p4;

  Decoder #(.select(4)) decoder_1 (
    .out10(decoder_1_out10), .out11(decoder_1_out11), .out12(decoder_1_out12), .out13(decoder_1_out13),
    .sel(ROM[11:8]), .en(Misc));  // open: out0, out1, out2, out3, out4, out5, out6, out7, out8, out9, out14, out15
  // Shift_Register #(.width(12), .length(4), .parallel("false")) shift_register_1: pin names not known; wires that end beside it: decoder_1_out12, Clock, Data, shift_register_1_p4
  S_R_Flip_Flop s_r_ff_1 (
    .S(decoder_1_out10), .R(decoder_1_out11), .clk(Clock), .Q(s_r_ff_1_q));  // open: reset, Qn, preset
  and and_1 (and_1_out, decoder_1_out13, Clock);
  assign ReadStack = s_r_ff_1_q ? shift_register_1_p4 : 12'bz;  // Controlled_Buffer controlled_buffer_1
  S_R_Flip_Flop #(.trigger("falling")) s_r_ff_2 (
    .S(and_1_out), .R(and_2_out), .clk(Clock), .Q(ResetCOUT));  // open: reset, Qn, preset
  and and_2 (and_2_out, ~and_1_out, Clock);  // AND_Gate
endmodule

module Count (
  input  MISC,
  input  [11:0] ROM,
  input  [11:0] DATA,
  input  SetCount,
  input  Clock,
  output [11:0] CNTOUT,
  output CNTOverflow
);

  wire and_1_out, and_2_out, decoder_1_out0, decoder_1_out1, decoder_1_out2, decoder_1_out3, decoder_1_out4,
       or_1_out, s_r_ff_1_q;
  wire [11:0] counter_1_q;

  Decoder #(.select(4)) decoder_1 (
    .out0(decoder_1_out0), .out1(decoder_1_out1), .out2(decoder_1_out2), .out3(decoder_1_out3),
    .out4(decoder_1_out4), .sel(ROM[11:8]), .en(MISC));  // open: out5, out6, out7, out8, out9, out10, out11, out12, out13, out14, out15
  Counter #(.width(12), .max('hfff)) counter_1 (
    .clr(and_1_out), .load(SetCount), .up(decoder_1_out0), .count(and_2_out), .clk(Clock), .D(DATA),
    .carry(CNTOverflow), .Q(counter_1_q));
  and and_1 (and_1_out, MISC, decoder_1_out2);
  and and_2 (and_2_out, MISC, or_1_out);
  or or_1 (or_1_out, decoder_1_out0, decoder_1_out1);
  assign CNTOUT = s_r_ff_1_q ? counter_1_q : 12'bz;  // Controlled_Buffer controlled_buffer_1
  S_R_Flip_Flop s_r_ff_1 (
    .S(decoder_1_out3), .R(decoder_1_out4), .clk(Clock), .Q(s_r_ff_1_q));  // open: reset, Qn, preset
endmodule

module Save_Load (
  input  SAVE,
  input  MISC,
  input  [11:0] ROM,
  input  Clk,
  output WriteEnable,
  output OutputEnable
);

  wire decoder_1_out5, decoder_1_out6;

  Decoder #(.select(4)) decoder_1 (
    .out5(decoder_1_out5), .out6(decoder_1_out6), .sel(ROM[11:8]), .en(MISC));  // open: out0, out1, out2, out3, out4, out7, out8, out9, out10, out11, out12, out13, out14, out15
  S_R_Flip_Flop s_r_ff_1 (
    .S(decoder_1_out5), .R(decoder_1_out6), .clk(Clk), .Q(OutputEnable));  // open: reset, Qn, preset

  assign WriteEnable = SAVE;
endmodule

module ReadCirc (
  input  MISC,
  input  [11:0] ROM,
  input  [11:0] ReadIn,
  input  Button,
  input  Clk,
  input  [11:0] GPInput,
  input  START,
  input  STOP,
  output [11:0] DATA,
  output HALT
);

  wire decoder_1_out7, decoder_1_out8, decoder_1_out9, decoder_1_out14, decoder_1_out15, or_1_out,
       s_r_ff_1_q, s_r_ff_2_q, s_r_ff_3_q;
  wire [11:0] register_1_q, register_2_q;

  Decoder #(.select(4)) decoder_1 (
    .out7(decoder_1_out7), .out8(decoder_1_out8), .out9(decoder_1_out9), .out14(decoder_1_out14),
    .out15(decoder_1_out15), .sel(ROM[11:8]), .en(MISC));  // open: out0, out1, out2, out3, out4, out5, out6, out10, out11, out12, out13
  S_R_Flip_Flop s_r_ff_1 (
    .S(decoder_1_out8), .R(decoder_1_out9), .clk(Clk), .Q(s_r_ff_1_q));  // open: reset, Qn, preset
  Register #(.width(12)) register_1 (.D(ReadIn), .en(s_r_ff_3_q), .clk(Button), .Q(register_1_q));  // open: clr
  S_R_Flip_Flop #(.trigger("falling")) s_r_ff_2 (
    .S(decoder_1_out14), .R(decoder_1_out15), .clk(Clk), .Q(s_r_ff_2_q));  // open: reset, Qn, preset
  Register #(.width(12)) register_2 (.D(GPInput), .en(1'b1), .clk(Clk), .Q(register_2_q));  // open: clr
  assign DATA = s_r_ff_1_q ? register_1_q : 12'bz;  // Controlled_Buffer controlled_buffer_1
  assign DATA = s_r_ff_2_q ? register_2_q : 12'bz;  // Controlled_Buffer controlled_buffer_2
  S_R_Flip_Flop #(.trigger("falling")) s_r_ff_3 (
    .S(decoder_1_out7), .R(1'b0), .clk(Clk), .Q(s_r_ff_3_q), .reset(or_1_out));  // open: Qn, preset
  or or_1 (or_1_out, Button, START, STOP);
  or or_2 (HALT, Button, s_r_ff_3_q);
endmodule
