// Logisim project COMPUTER_One.circ as structural Verilog: 5 circuits, main circuit main
module main (
);

  wire AccumulatorEquals, AccuOut, ACUEQU, ADD, Carry, CarryIn, Clk, CNT, CNTOVER, CNTOVERFLOW, DataEquals,
       DATEQU, FLAG, IsCarry, IsZero, jmp_1_pcload, JMPACUEQU, JMPCARRY, JMPCNTOVER, JMPDATA, JMPDATEQU,
       JMPZERO, JUMP, LOAD, POWER, register_1_q, ResetAccu, RomToData, SAVE, SetA, SetCount, SetEqualREG,
       Sub, WriteOut, Zero;
  wire [7:0] binairy_to_bcd_converter_1_p1, counter_1_q, Data, jmp_1_pcin, ROMData;
  wire [11:8] rom_1_data;

  JMP jmp_1 (
    .JMP(JUMP), .JMPZERO(JMPZERO), .ZERO(Zero), .JMPCARRY(JMPCARRY), .CARRY(Carry), .JMPDATA(JMPDATA),
    .JMPACUEQU(JMPACUEQU), .ACUEQU(ACUEQU), .JMPDATEQU(JMPDATEQU), .DATEQU(DATEQU), .JMPCNTOVER(JMPCNTOVER),
    .CNTOVER(CNTOVER), .ROM(ROMData), .DATA(Data), .PCIn(jmp_1_pcin), .PCLoad(jmp_1_pcload));
  Count count_1 (
    .Count(CNT), .ROM(ROMData), .DATA(Data), .SetCount(SetCount), .Clock(Clk), .CNTOUT(Data),
    .CNTOverflow(CNTOVERFLOW));
  Counter #(.ongoal("stay"), .trigger("falling")) counter_1 (
    .clr(1'b0), .load(jmp_1_pcload), .up(1'b1), .count(POWER), .clk(Clk), .D(jmp_1_pcin), .Q(counter_1_q));  // open: carry
  Clock clock_1 (.out(Clk));
  FLG flg_1 (
    .FLG(FLAG), .ROM(ROMData), .IsCarry(IsCarry), .IsZero(IsZero), .AccumulatorEquals(AccumulatorEquals),
    .DataEquals(DataEquals), .Clock(Clk), .CNTOverflow(CNTOVERFLOW), .WriteOut(WriteOut), .AccuOut(AccuOut),
    .RomToData(RomToData), .Carry(Carry), .Zero(Zero), .Sub(Sub), .CarryIn(CarryIn),
    .ResetAccumulator(ResetAccu), .AcuEqu(ACUEQU), .DatEqu(DATEQU), .CNTOverFlag(CNTOVER), .Power(POWER));
  ALU alu_1 (
    .Sub(Sub), .CarryIn(CarryIn), .Ain(Data), .SetA(SetA), .AccumulatorOut(AccuOut), .Add(ADD),
    .ResetAcum(ResetAccu), .SetEqualREG(SetEqualREG), .Clock(Clk), .Accumulator(Data),
    .AccumulatorIsZero(IsZero), .CarryOut(IsCarry), .DataEquals(DataEquals),
    .AccumulatorEquals(AccumulatorEquals));
  ROM #(.dataWidth(12)) rom_1 (.addr(counter_1_q), .data({rom_1_data, ROMData}));
  LED led_1 (.in(Zero));
  LED led_2 (.in(WriteOut));
  LED led_3 (.in(Sub));
  LED led_4 (.in(CarryIn));
  RAM ram_1 (.addr(ROMData), .we(SAVE), .oe(register_1_q), .clk(Clk), .data(Data));
  Register #(.width(1)) register_1 (.D(ROMData[4]), .en(LOAD), .clk(Clk), .Q(register_1_q));  // open: clr
  LED led_5 (.in(AccuOut));
  LED led_6 (.in(ResetAccu));
  Decoder #(.select(4), .enable("false")) decoder_1 (
    .out1(FLAG), .out2(JUMP), .out3(JMPDATA), .out4(JMPZERO), .out5(JMPCARRY), .out6(JMPACUEQU),
    .out7(JMPDATEQU), .out8(ADD), .out9(SetA), .out10(SetEqualREG), .out11(SetCount), .out12(SAVE),
    .out13(CNT), .out14(LOAD), .out15(JMPCNTOVER), .sel(rom_1_data));  // open: out0
  LED led_7 (.in(RomToData));
  Hex_Digit_Display hex_digit_display_1 (.value(Data[7:4]), .dp(Data[0]));
  assign Data = RomToData ? ROMData : 8'bz;  // Controlled_Buffer controlled_buffer_1
  Pull_Resistor pull_resistor_1 (.node(Data));
  LED led_8 (.in(Carry));
  LED led_9 (.in(DATEQU));
  LED led_10 (.in(ACUEQU));
  Hex_Digit_Display hex_digit_display_2 (.value(Data[3:0]));  // open: dp
  LED led_11 (.in(POWER));
  LED led_12 (.in(CNTOVER));
  Counter #(.width(12), .max('hfff)) counter_2 (
    .clr(1'b0), .load(1'b0), .up(1'b1), .count(POWER), .clk(Clk));  // open: D, carry, Q
  _7_Segment_Display u_7_segment_display_1 ();  // open: g, f, a, b, e, d, c, dp
  // BCD_to_7_Segment_decoder bcd_to_7_segment_decoder_1: pin names not known
  _7_Segment_Display u_7_segment_display_2 ();  // open: g, f, a, b, e, d, c, dp
  // BCD_to_7_Segment_decoder bcd_to_7_segment_decoder_2: pin names not known
  // Binairy_to_BCD_converter #(.binvalue(8)) binairy_to_bcd_converter_1: pin names not known; wires that end beside it: binairy_to_bcd_converter_1_p1
  Register register_2 (.D(Data), .en(WriteOut), .clk(Clk), .Q(binairy_to_bcd_converter_1_p1));  // open: clr
  _7_Segment_Display u_7_segment_display_3 ();  // open: g, f, a, b, e, d, c, dp
  // BCD_to_7_Segment_decoder bcd_to_7_segment_decoder_3: pin names not known
  // Pins of 1 and 4 bits meet at Data[3:0]

  // Notes on the sheet:
  //   contents of rom_1 (hex, n*v repeats v):
  //   140 90f 800 903 180 160 50a 800 d00 206 0 d30 150 100 1f0
endmodule

module JMP (
  input  JMP,
  input  JMPZERO,
  input  ZERO,
  input  JMPCARRY,
  input  CARRY,
  input  JMPDATA,
  input  JMPACUEQU,
  input  ACUEQU,
  input  JMPDATEQU,
  input  DATEQU,
  input  JMPCNTOVER,
  input  CNTOVER,
  input  [7:0] ROM,
  input  [7:0] DATA,
  output [7:0] PCIn,
  output PCLoad
);

  wire and_1_out, and_2_out, and_3_out, and_4_out, and_5_out;

  and and_1 (and_1_out, JMPZERO, ZERO);
  and and_2 (and_2_out, JMPCARRY, CARRY);
  and and_3 (and_3_out, JMPACUEQU, ACUEQU);
  and and_4 (and_4_out, JMPDATEQU, DATEQU);
  and and_5 (and_5_out, JMPCNTOVER, CNTOVER);
  Multiplexer #(.width(8), .enable("false")) multiplexer_1 (.in0(ROM), .in1(DATA), .out(PCIn), .sel(JMPDATA));
  or or_1 (PCLoad, JMP, and_1_out, and_2_out, JMPDATA, and_3_out, and_4_out, and_5_out);
endmodule

module ALU (
  input  Sub,
  input  CarryIn,
  input  [7:0] Ain,
  input  SetA,
  input  AccumulatorOut,
  input  Add,
  input  ResetAcum,
  input  SetEqualREG,
  input  Clock,
  output [7:0] Accumulator,
  output AccumulatorIsZero,
  output CarryOut,
  output DataEquals,
  output AccumulatorEquals
);

  wire adder_1_cout, or_1_out, subtractor_1_bout;
  wire [7:0] adder_1_out, multiplexer_2_out, register_1_q, register_2_q, register_3_q, subtractor_1_out;

  Register register_1 (.D(Ain), .en(SetEqualREG), .clk(Clock), .Q(register_1_q));  // open: clr
  Register register_2 (.D(Ain), .en(SetA), .clk(Clock), .Q(register_2_q));  // open: clr
  Subtractor subtractor_1 (
    .a(register_3_q), .b(register_2_q), .out(subtractor_1_out), .bin(CarryIn), .bout(subtractor_1_bout));
  Multiplexer #(.enable("false")) multiplexer_1 (
    .in0(adder_1_cout), .in1(subtractor_1_bout), .out(CarryOut), .sel(Sub));
  Comparator comparator_1 (.a(Ain), .b(register_1_q), .eq(DataEquals));  // open: gt, lt
  Adder adder_1 (.a(register_3_q), .b(register_2_q), .out(adder_1_out), .cin(CarryIn), .cout(adder_1_cout));
  Register register_3 (.D(multiplexer_2_out), .en(Add), .clk(Clock), .Q(register_3_q), .clr(ResetAcum));
  Multiplexer #(.width(8), .enable("false")) multiplexer_2 (
    .in0(adder_1_out), .in1(subtractor_1_out), .out(multiplexer_2_out), .sel(Sub));
  assign Accumulator = AccumulatorOut ? register_3_q : 8'bz;  // Controlled_Buffer controlled_buffer_1
  Comparator comparator_2 (.a(register_3_q), .b(register_1_q), .eq(AccumulatorEquals));  // open: gt, lt
  or or_1 (or_1_out, register_3_q[0], register_3_q[1], register_3_q[2], register_3_q[3], register_3_q[4], register_3_q[5], register_3_q[6], register_3_q[7]);
  not not_1 (AccumulatorIsZero, or_1_out);
endmodule

module FLG (
  input  FLG,
  input  [7:0] ROM,
  input  IsCarry,
  input  IsZero,
  input  AccumulatorEquals,
  input  DataEquals,
  input  Clock,
  input  CNTOverflow,
  output WriteOut,
  output AccuOut,
  output RomToData,
  output Carry,
  output Zero,
  output Sub,
  output CarryIn,
  output ResetAccumulator,
  output AcuEqu,
  output DatEqu,
  output CNTOverFlag,
  output Power
);

  wire decoder_1_out1, decoder_1_out2, decoder_1_out3, decoder_1_out4, decoder_1_out5, decoder_1_out6,
       decoder_1_out7, decoder_1_out8, decoder_1_out9, decoder_1_out10, decoder_1_out11, decoder_1_out13,
       decoder_1_out14, decoder_1_out15;

  Decoder #(.select(4)) decoder_1 (
    .out0(WriteOut), .out1(decoder_1_out1), .out2(decoder_1_out2), .out3(decoder_1_out3),
    .out4(decoder_1_out4), .out5(decoder_1_out5), .out6(decoder_1_out6), .out7(decoder_1_out7),
    .out8(decoder_1_out8), .out9(decoder_1_out9), .out10(decoder_1_out10), .out11(decoder_1_out11),
    .out12(ResetAccumulator), .out13(decoder_1_out13), .out14(decoder_1_out14), .out15(decoder_1_out15),
    .sel(ROM[7:4]), .en(FLG));
  S_R_Flip_Flop AccuOutf (
    .S(decoder_1_out2), .R(decoder_1_out3), .clk(Clock), .Q(AccuOut), .reset(decoder_1_out1));  // open: Qn, preset
  S_R_Flip_Flop RomToDataf (
    .S(decoder_1_out4), .R(decoder_1_out5), .clk(Clock), .Q(RomToData), .reset(decoder_1_out1));  // open: Qn, preset
  S_R_Flip_Flop Carryf (
    .S(IsCarry), .R(decoder_1_out6), .clk(Clock), .Q(Carry), .reset(decoder_1_out1));  // open: Qn, preset
  S_R_Flip_Flop Zerof (
    .S(IsZero), .R(decoder_1_out7), .clk(Clock), .Q(Zero), .reset(decoder_1_out1));  // open: Qn, preset
  S_R_Flip_Flop Subf (
    .S(decoder_1_out8), .R(decoder_1_out9), .clk(Clock), .Q(Sub), .reset(decoder_1_out1));  // open: Qn, preset
  S_R_Flip_Flop CarryInf (
    .S(decoder_1_out10), .R(decoder_1_out11), .clk(Clock), .Q(CarryIn), .reset(decoder_1_out1));  // open: Qn, preset
  S_R_Flip_Flop AccumEqualsf (
    .S(AccumulatorEquals), .R(decoder_1_out13), .clk(Clock), .Q(AcuEqu), .reset(decoder_1_out1));  // open: Qn, preset
  S_R_Flip_Flop s_r_ff_1 (
    .S(CNTOverflow), .R(decoder_1_out14), .clk(Clock), .Q(CNTOverFlag), .reset(decoder_1_out1));  // open: Qn, preset
  S_R_Flip_Flop Powerf (
    .S(decoder_1_out15), .R(1'b0), .clk(Clock), .reset(decoder_1_out1), .Qn(Power));  // open: Q, preset

  assign DatEqu = DataEquals;
endmodule

module Count (
  input  Count,
  input  [7:0] ROM,
  input  [7:0] DATA,
  input  SetCount,
  input  Clock,
  output [7:0] CNTOUT,
  output CNTOverflow
);

  wire and_1_out, and_2_out, decoder_1_out0, decoder_1_out1, decoder_1_out2, decoder_1_out3, decoder_1_out4,
       or_1_out, s_r_ff_1_q;
  wire [7:0] counter_1_q;

  Decoder #(.select(3)) decoder_1 (
    .out0(decoder_1_out0), .out1(decoder_1_out1), .out2(decoder_1_out2), .out3(decoder_1_out3),
    .out4(decoder_1_out4), .sel(ROM[6:4]), .en(Count));  // open: out5, out6, out7
  Counter counter_1 (
    .clr(and_1_out), .load(SetCount), .up(decoder_1_out0), .count(and_2_out), .clk(Clock), .D(DATA),
    .carry(CNTOverflow), .Q(counter_1_q));
  and and_1 (and_1_out, Count, decoder_1_out2);
  and and_2 (and_2_out, Count, or_1_out);
  or or_1 (or_1_out, decoder_1_out0, decoder_1_out1);
  assign CNTOUT = s_r_ff_1_q ? counter_1_q : 8'bz;  // Controlled_Buffer controlled_buffer_1
  S_R_Flip_Flop s_r_ff_1 (
    .S(decoder_1_out3), .R(decoder_1_out4), .clk(Clock), .Q(s_r_ff_1_q));  // open: reset, Qn, preset
endmodule
