// Logisim project COMPUTER_Three.circ as structural Verilog: 8 circuits, main circuit main
module main (
);

  wire AccumulatorEquals, AccuOut, ACUEQU, AL, and_1_out, and_2_out, and_3_out, and_4_out, and_5_out, Borrow,
       Btn, Carry, CB, Clk, clock_1_out, clock_2_out, CNTOVER, CNTOVERFLOW, COUT, DATEQU, FLAG, GPO1, GPO2,
       Halt, IsBorrow, IsCarry, IsZero, JMPACUEQU, JMPCB, JMPCNTOVER, JMPDATA, JMPDATEQU, JMPZERO, JUMP,
       MISC, multiplexer_1_out, not_1_out, not_2_out, not_3_out, not_4_out, not_5_out, not_6_out, or_1_out,
       or_2_out, or_3_out, OUTF0, OutputEnable, PCLoad, POWER, PrgOrMem, RESET, ResetCOUT, RomToData, SAVE,
       SetA, SetCount, SetEqualREG, START, WriteEnable, WriteOut, Zero;
  wire [7:0] Add, Data, GPInput, GPOut1, GPOut2, multiplexer_2_out, multiplexer_3_out, Out0, PCIn,
       ProgramCount, ReadIn;
  wire [11:0] Dat, Instructions, ram_1_data;
  wire [11:8] controlled_buffer_3_out;

  and and_1 (and_1_out, POWER, not_1_out, not_2_out);
  Multiplexer #(.enable("false")) multiplexer_1 (.in0(Carry), .in1(Borrow), .out(multiplexer_1_out), .sel(CB));
  not not_1 (not_1_out, Halt);
  not not_2 (not_2_out, PrgOrMem);
  Counter #(.ongoal("stay"), .trigger("falling")) counter_1 (
    .clr(1'b0), .load(PCLoad), .up(1'b1), .count(and_1_out), .clk(Clk), .D(PCIn), .Q(ProgramCount));  // open: carry
  JMP jmp_1 (
    .JMP(JUMP), .JMPZERO(JMPZERO), .ZERO(Zero), .JMPCARRYBORROW(JMPCB), .CARRYBORROW(multiplexer_1_out),
    .JMPDATA(JMPDATA), .JMPACUEQU(JMPACUEQU), .ACUEQU(ACUEQU), .JMPDATEQU(JMPDATEQU), .DATEQU(DATEQU),
    .JMPCNTOVER(JMPCNTOVER), .CNTOVER(CNTOVER), .ROM(Instructions[7:0]), .DATA(Data), .PCLoad(PCLoad),
    .PCIn(PCIn));
  FLG flg_1 (
    .FLG(FLAG), .ROM(Instructions[7:0]), .IsCarry(IsCarry), .IsZero(IsZero),
    .AccumulatorEquals(AccumulatorEquals), .CNTOverflow(CNTOVERFLOW), .Borrow(IsBorrow), .START(START),
    .Clock(Clk), .WriteOut(OUTF0), .GPO1(GPO1), .GPO2(GPO2), .AccuOut(AccuOut), .RomToData(RomToData),
    .Carry(Carry), .Zero(Zero), .AcuEqu(ACUEQU), .CorB(CB), .CNTOverFlag(CNTOVER), .BorrowFlag(Borrow),
    .Power(POWER), .RESET(RESET));
  ALU alu_1 (
    .ALU(AL), .DATAIn(Data), .SetA(SetA), .AccumulatorOut(AccuOut), .ROM(Instructions[7:0]),
    .SetEqualREG(SetEqualREG), .Clock(Clk), .DATAOut(Data), .AccumulatorIsZero(IsZero), .CarryOut(IsCarry),
    .BorrowOut(IsBorrow), .DataEquals(DATEQU), .AccumulatorEquals(AccumulatorEquals));
  Counter #(.trigger("falling")) counter_2 (
    .clr(1'b0), .load(1'b0), .up(1'b1), .count(not_3_out), .clk(clock_1_out), .carry(START), .Q(Add));  // open: D
  not not_3 (not_3_out, POWER);
  Clock clock_1 (.out(clock_1_out));
  Decoder #(.select(4)) decoder_1 (
    .out1(FLAG), .out2(JUMP), .out3(JMPDATA), .out4(JMPZERO), .out5(JMPCB), .out6(JMPACUEQU),
    .out7(JMPDATEQU), .out8(JMPCNTOVER), .out9(AL), .out10(SetA), .out11(SetEqualREG), .out12(SetCount),
    .out13(COUT), .out14(SAVE), .out15(MISC), .sel(Instructions[11:8]), .en(PrgOrMem));  // open: out0
  ROM #(.dataWidth(12)) rom_1 (.addr(Add), .data(Dat));
  Stack stack_1 (
    .Misc(MISC), .ROM(Instructions[7:0]), .Data(Data), .Clock(Clk), .ReadStack(Data), .ResetCOUT(ResetCOUT));
  Count count_1 (
    .MISC(MISC), .ROM(Instructions[7:0]), .DATA(Data), .SetCount(SetCount), .Clock(Clk), .CNTOUT(Data),
    .CNTOverflow(CNTOVERFLOW));
  Save_Load save_load_1 (
    .WriteEnable(WriteEnable), .SAVE(SAVE), .ROM(Instructions[7:0]), .OutputEnable(OutputEnable), .Clk(Clk),
    .MISC(MISC));
  ReadCirc readcirc_1 (
    .MISC(MISC), .ROM(Instructions[7:0]), .ReadIn(ReadIn), .Button(Btn), .Clk(Clk), .GPInput(GPInput),
    .DATA(Data), .HALT(Halt));
  // BCD_to_7_Segment_decoder bcd_to_7_segment_decoder_1: pin names not known
  _7_Segment_Display u_7_segment_display_1 ();  // open: g, f, a, b, e, d, c, dp
  // Binairy_to_BCD_converter #(.binvalue(8)) binairy_to_bcd_converter_1: pin names not known; wires that end beside it: Out0
  _7_Segment_Display u_7_segment_display_2 ();  // open: g, f, a, b, e, d, c, dp
  // BCD_to_7_Segment_decoder bcd_to_7_segment_decoder_2: pin names not known
  // Binairy_to_BCD_converter #(.binvalue(8)) binairy_to_bcd_converter_2: pin names not known; wires that end beside it: ReadIn
  DipSwitch dipswitch_1 (
    .sw1(ReadIn[7]), .sw2(ReadIn[6]), .sw3(ReadIn[5]), .sw4(ReadIn[4]), .sw5(ReadIn[3]), .sw6(ReadIn[2]),
    .sw7(ReadIn[1]), .sw8(ReadIn[0]));
  Button button_1 (.out(Btn));
  DipSwitch dipswitch_2 (
    .sw1(GPInput[7]), .sw2(GPInput[6]), .sw3(GPInput[5]), .sw4(GPInput[4]), .sw5(GPInput[3]),
    .sw6(GPInput[2]), .sw7(GPInput[1]), .sw8(GPInput[0]));
  Multiplexer #(.width(8), .enable("false")) multiplexer_2 (
    .in0(ProgramCount), .in1(Instructions[7:0]), .out(multiplexer_2_out), .sel(PrgOrMem));
  and and_2 (and_2_out, PrgOrMem, WriteEnable);
  or or_1 (or_1_out, OutputEnable, not_4_out);
  not not_4 (not_4_out, PrgOrMem);
  // BCD_to_7_Segment_decoder bcd_to_7_segment_decoder_3: pin names not known
  _7_Segment_Display u_7_segment_display_3 ();  // open: g, f, a, b, e, d, c, dp
  // BCD_to_7_Segment_decoder bcd_to_7_segment_decoder_4: pin names not known
  _7_Segment_Display u_7_segment_display_4 ();  // open: g, f, a, b, e, d, c, dp
  _7_Segment_Display u_7_segment_display_5 ();  // open: g, f, a, b, e, d, c, dp
  _7_Segment_Display u_7_segment_display_6 ();  // open: g, f, a, b, e, d, c, dp
  // BCD_to_7_Segment_decoder bcd_to_7_segment_decoder_5: pin names not known
  // BCD_to_7_Segment_decoder bcd_to_7_segment_decoder_6: pin names not known
  TTY #(.rows(4), .cols(20)) tty_1 (.data(Data[6:0]), .clk(Clk), .we(COUT), .clr(ResetCOUT));
  Multiplexer #(.width(8), .enable("false")) multiplexer_3 (
    .in0(Add), .in1(multiplexer_2_out), .out(multiplexer_3_out), .sel(POWER));
  RAM #(.dataWidth(12), .trigger("high")) ram_1 (
    .addr(multiplexer_3_out), .we(or_2_out), .oe(and_3_out), .data(ram_1_data));
  or or_2 (or_2_out, ~POWER, and_2_out);  // OR_Gate
  and and_3 (and_3_out, POWER, or_1_out);
  Hex_Digit_Display hex_digit_display_1 (.value(ProgramCount[7:4]), .dp(ProgramCount[4]));
  Hex_Digit_Display hex_digit_display_2 (.value(ProgramCount[3:0]));  // open: dp
  DotMatrix #(.inputtype("row"), .matrixcols(8), .matrixrows(1)) dotmatrix_1 (.row0(GPOut1));
  DotMatrix #(.inputtype("row"), .matrixcols(8), .matrixrows(1)) dotmatrix_2 (.row0(GPOut2));
  LED led_1 (.in(WriteOut));
  LED led_2 (.in(Carry));
  LED led_3 (.in(Borrow));
  LED led_4 (.in(Zero));
  Hex_Digit_Display hex_digit_display_3 (.value(Instructions[7:4]), .dp(Instructions[0]));
  // Hex_Digit_Display hex_digit_display_4: pin names not known; wires that end beside it: Instructions[11:8]
  LED led_5 (.in(AccuOut));
  LED led_6 (.in(DATEQU));
  LED led_7 (.in(CB));
  LED led_8 (.in(POWER));
  Hex_Digit_Display hex_digit_display_5 (.value(Instructions[3:0]));  // open: dp
  Hex_Digit_Display hex_digit_display_6 (.value(Data[7:4]), .dp(Data[4]));
  not not_5 (not_5_out, POWER);
  assign ram_1_data = not_5_out ? Dat : 12'bz;  // Controlled_Buffer controlled_buffer_1
  and and_4 (and_4_out, WriteEnable, PrgOrMem);
  assign ram_1_data = and_4_out ? {controlled_buffer_3_out, Data} : 12'bz;  // Controlled_Buffer controlled_buffer_2
  and and_5 (and_5_out, PrgOrMem, OutputEnable);
  Pull_Resistor pull_resistor_1 (.node(ram_1_data));
  LED led_9 (.in(RomToData));
  LED led_10 (.in(ACUEQU));
  LED led_11 (.in(CNTOVER));
  LED led_12 (.in(Halt));
  Hex_Digit_Display hex_digit_display_7 (.value(Data[3:0]));  // open: dp
  assign {controlled_buffer_3_out, Data} = and_5_out ? ram_1_data : 12'bz;  // Controlled_Buffer controlled_buffer_3
  T_Flip_Flop t_ff_1 (.T(1'b1), .clk(Clk), .Q(PrgOrMem));  // open: Qn, reset, preset
  Register #(.width(12)) register_1 (.D(ram_1_data), .en(not_6_out), .clk(Clk), .Q(Instructions));  // open: clr
  not not_6 (not_6_out, PrgOrMem);
  Register register_2 (.D(Data), .en(OUTF0), .clk(Clk), .Q(Out0));  // open: clr
  Register register_3 (.D(Data), .en(GPO1), .clk(Clk), .Q(GPOut1));  // open: clr
  Register register_4 (.D(Data), .en(GPO2), .clk(Clk), .Q(GPOut2));  // open: clr
  assign Data = RomToData ? Instructions[7:0] : 8'bz;  // Controlled_Buffer controlled_buffer_4
  Pull_Resistor pull_resistor_2 (.node(Data));
  Clock clock_2 (.out(clock_2_out));
  and and_6 (Clk, clock_2_out, ~or_3_out);  // AND_Gate
  or or_3 (or_3_out, Halt, ~POWER);  // OR_Gate
  // Pins of 1 and 4 bits meet at ProgramCount[7:4]
  // Pins of 1 and 4 bits meet at Instructions[3:0]
  // Pins of 1 and 4 bits meet at Data[7:4]

  // Other names for the same wires on the sheet: ROMData[7:0] = Instructions[7:0]

  // Notes on the sheet:
  //   contents of rom_1 (hex, n*v repeats v):
  //   fd0 150 d69 d6c d69 d70 1e0 f70 fd0 1f0
endmodule

module JMP (
  input  JMP,
  input  JMPZERO,
  input  ZERO,
  input  JMPCARRYBORROW,
  input  CARRYBORROW,
  input  JMPDATA,
  input  JMPACUEQU,
  input  ACUEQU,
  input  JMPDATEQU,
  input  DATEQU,
  input  JMPCNTOVER,
  input  CNTOVER,
  input  [7:0] ROM,
  input  [7:0] DATA,
  output PCLoad,
  output [7:0] PCIn
);

  wire and_1_out, and_2_out, and_3_out, and_4_out, and_5_out;

  and and_1 (and_1_out, JMPZERO, ZERO);
  and and_2 (and_2_out, JMPCARRYBORROW, CARRYBORROW);
  and and_3 (and_3_out, JMPACUEQU, ACUEQU);
  and and_4 (and_4_out, JMPDATEQU, DATEQU);
  and and_5 (and_5_out, JMPCNTOVER, CNTOVER);
  or or_1 (PCLoad, JMP, and_1_out, and_2_out, JMPDATA, and_3_out, and_4_out, and_5_out);
  Multiplexer #(.width(8), .enable("false")) multiplexer_1 (.in0(ROM), .in1(DATA), .out(PCIn), .sel(JMPDATA));
endmodule

module ALU (
  input  ALU,
  input  [7:0] DATAIn,
  input  SetA,
  input  AccumulatorOut,
  input  [7:0] ROM,
  input  SetEqualREG,
  input  Clock,
  output [7:0] DATAOut,
  output AccumulatorIsZero,
  output CarryOut,
  output BorrowOut,
  output DataEquals,
  output AccumulatorEquals
);

  wire and_1_out, and_2_out, BorrowIn_q, CarryIn_q, decoder_1_out0, decoder_1_out1, decoder_1_out2,
       decoder_1_out3, decoder_1_out4, decoder_1_out5, decoder_1_out6, decoder_1_out7, or_1_out, or_2_out;
  wire [7:0] A_q, Accumulator_q, adder_1_out, controlled_buffer_1_out, nand_1_out, register_1_q,
       subtractor_1_out;

  Decoder #(.select(3)) decoder_1 (
    .out0(decoder_1_out0), .out1(decoder_1_out1), .out2(decoder_1_out2), .out3(decoder_1_out3),
    .out4(decoder_1_out4), .out5(decoder_1_out5), .out6(decoder_1_out6), .out7(decoder_1_out7),
    .sel(ROM[6:4]), .en(ALU));
  Register A (.D(DATAIn), .en(SetA), .clk(Clock), .Q(A_q));  // open: clr
  Register register_1 (.D(DATAIn), .en(SetEqualREG), .clk(Clock), .Q(register_1_q));  // open: clr
  S_R_Flip_Flop BorrowIn (
    .S(decoder_1_out6), .R(decoder_1_out7), .clk(Clock), .Q(BorrowIn_q));  // open: reset, Qn, preset
  S_R_Flip_Flop CarryIn (
    .S(decoder_1_out4), .R(decoder_1_out5), .clk(Clock), .Q(CarryIn_q));  // open: reset, Qn, preset
  and and_1 (and_1_out, decoder_1_out3, ALU);
  Comparator comparator_1 (.a(DATAIn), .b(register_1_q), .eq(DataEquals));  // open: gt, lt
  Adder adder_1 (.a(Accumulator_q), .b(A_q), .out(adder_1_out), .cin(CarryIn_q), .cout(CarryOut));
  assign nand_1_out = ~(Accumulator_q & A_q);  // NAND_Gate nand_1, 8 bits wide
  or or_1 (or_1_out, decoder_1_out1, decoder_1_out0, decoder_1_out2);
  Subtractor subtractor_1 (.a(Accumulator_q), .b(A_q), .out(subtractor_1_out), .bin(BorrowIn_q), .bout(BorrowOut));
  assign controlled_buffer_1_out = decoder_1_out1 ? subtractor_1_out : 8'bz;  // Controlled_Buffer controlled_buffer_1
  assign controlled_buffer_1_out = decoder_1_out0 ? adder_1_out : 8'bz;  // Controlled_Buffer controlled_buffer_2
  assign controlled_buffer_1_out = decoder_1_out2 ? nand_1_out : 8'bz;  // Controlled_Buffer controlled_buffer_3
  and and_2 (and_2_out, or_1_out, ALU);
  Pull_Resistor pull_resistor_1 (.node(controlled_buffer_1_out));
  Register Accumulator (.D(controlled_buffer_1_out), .en(and_2_out), .clk(Clock), .Q(Accumulator_q), .clr(and_1_out));
  assign DATAOut = AccumulatorOut ? Accumulator_q : 8'bz;  // Controlled_Buffer controlled_buffer_4
  Comparator comparator_2 (.a(Accumulator_q), .b(register_1_q), .eq(AccumulatorEquals));  // open: gt, lt
  or or_2 (or_2_out, Accumulator_q[0], Accumulator_q[1], Accumulator_q[2], Accumulator_q[3], Accumulator_q[4], Accumulator_q[5], Accumulator_q[6], Accumulator_q[7]);
  not not_1 (AccumulatorIsZero, or_2_out);
endmodule

module FLG (
  input  FLG,
  input  [7:0] ROM,
  input  IsCarry,
  input  IsZero,
  input  AccumulatorEquals,
  input  CNTOverflow,
  input  Borrow,
  input  START,
  input  Clock,
  output WriteOut,
  output GPO1,
  output GPO2,
  output AccuOut,
  output RomToData,
  output Carry,
  output Zero,
  output AcuEqu,
  output CorB,
  output CNTOverFlag,
  output BorrowFlag,
  output Power,
  output RESET
);

  wire decoder_1_out3, decoder_1_out4, decoder_1_out5, decoder_1_out6, decoder_1_out7, decoder_1_out8,
       decoder_1_out9, decoder_1_out10, decoder_1_out11, decoder_1_out12, decoder_1_out13, decoder_1_out15;

  Decoder #(.select(4)) decoder_1 (
    .out0(WriteOut), .out1(GPO1), .out2(GPO2), .out3(decoder_1_out3), .out4(decoder_1_out4),
    .out5(decoder_1_out5), .out6(decoder_1_out6), .out7(decoder_1_out7), .out8(decoder_1_out8),
    .out9(decoder_1_out9), .out10(decoder_1_out10), .out11(decoder_1_out11), .out12(decoder_1_out12),
    .out13(decoder_1_out13), .out14(RESET), .out15(decoder_1_out15), .sel(ROM[7:4]), .en(FLG));
  S_R_Flip_Flop AccuOutf (
    .S(decoder_1_out3), .R(decoder_1_out4), .clk(Clock), .Q(AccuOut), .reset(RESET));  // open: Qn, preset
  S_R_Flip_Flop RomToDataf (
    .S(decoder_1_out5), .R(decoder_1_out6), .clk(Clock), .Q(RomToData), .reset(RESET));  // open: Qn, preset
  S_R_Flip_Flop Carryf (.S(IsCarry), .R(decoder_1_out7), .clk(Clock), .Q(Carry), .reset(RESET));  // open: Qn, preset
  S_R_Flip_Flop Zerof (.S(IsZero), .R(decoder_1_out8), .clk(Clock), .Q(Zero), .reset(RESET));  // open: Qn, preset
  S_R_Flip_Flop AccumEqualsf (
    .S(AccumulatorEquals), .R(decoder_1_out9), .clk(Clock), .Q(AcuEqu), .reset(RESET));  // open: Qn, preset
  S_R_Flip_Flop s_r_ff_1 (
    .S(decoder_1_out12), .R(decoder_1_out13), .clk(Clock), .Q(CorB), .reset(RESET));  // open: Qn, preset
  S_R_Flip_Flop CNTOVERf (
    .S(CNTOverflow), .R(decoder_1_out10), .clk(Clock), .Q(CNTOverFlag), .reset(RESET));  // open: Qn, preset
  S_R_Flip_Flop Borrowf (
    .S(Borrow), .R(decoder_1_out11), .clk(Clock), .Q(BorrowFlag), .reset(RESET));  // open: Qn, preset
  S_R_Flip_Flop Powerf (.R(decoder_1_out15), .clk(Clock), .Q(Power), .preset(START));  // open: S, reset, Qn
endmodule

module Count (
  input  MISC,
  input  [7:0] ROM,
  input  [7:0] DATA,
  input  SetCount,
  input  Clock,
  output [7:0] CNTOUT,
  output CNTOverflow
);

  wire and_1_out, and_2_out, decoder_1_out0, decoder_1_out1, decoder_1_out2, decoder_1_out3, decoder_1_out4,
       or_1_out, s_r_ff_1_q;
  wire [7:0] counter_1_q;

  Decoder #(.select(4)) decoder_1 (
    .out0(decoder_1_out0), .out1(decoder_1_out1), .out2(decoder_1_out2), .out3(decoder_1_out3),
    .out4(decoder_1_out4), .sel(ROM[7:4]), .en(MISC));  // open: out5, out6, out7, out8, out9, out10, out11, out12, out13, out14, out15
  Counter counter_1 (
    .clr(and_1_out), .load(SetCount), .up(decoder_1_out0), .count(and_2_out), .clk(Clock), .D(DATA),
    .carry(CNTOverflow), .Q(counter_1_q));
  and and_1 (and_1_out, MISC, decoder_1_out2);
  and and_2 (and_2_out, MISC, or_1_out);
  or or_1 (or_1_out, decoder_1_out0, decoder_1_out1);
  assign CNTOUT = s_r_ff_1_q ? counter_1_q : 8'bz;  // Controlled_Buffer controlled_buffer_1
  S_R_Flip_Flop s_r_ff_1 (
    .S(decoder_1_out3), .R(decoder_1_out4), .clk(Clock), .Q(s_r_ff_1_q));  // open: reset, Qn, preset
endmodule

module Save_Load (
  input  SAVE,
  input  MISC,
  input  [7:0] ROM,
  input  Clk,
  output WriteEnable,
  output OutputEnable
);

  wire decoder_1_out5, decoder_1_out6;

  Decoder #(.select(4)) decoder_1 (
    .out5(decoder_1_out5), .out6(decoder_1_out6), .sel(ROM[7:4]), .en(MISC));  // open: out0, out1, out2, out3, out4, out7, out8, out9, out10, out11, out12, out13, out14, out15
  S_R_Flip_Flop s_r_ff_1 (
    .S(decoder_1_out5), .R(decoder_1_out6), .clk(Clk), .Q(OutputEnable));  // open: reset, Qn, preset

  assign WriteEnable = SAVE;
endmodule

module ReadCirc (
  input  MISC,
  input  [7:0] ROM,
  input  [7:0] ReadIn,
  input  Button,
  input  Clk,
  input  [7:0] GPInput,
  output [7:0] DATA,
  output HALT
);

  wire decoder_1_out7, decoder_1_out8, decoder_1_out9, decoder_1_out14, decoder_1_out15, s_r_ff_1_q,
       s_r_ff_2_q, s_r_ff_3_q;
  wire [7:0] register_1_q, register_2_q;

  Decoder #(.select(4)) decoder_1 (
    .out7(decoder_1_out7), .out8(decoder_1_out8), .out9(decoder_1_out9), .out14(decoder_1_out14),
    .out15(decoder_1_out15), .sel(ROM[7:4]), .en(MISC));  // open: out0, out1, out2, out3, out4, out5, out6, out10, out11, out12, out13
  S_R_Flip_Flop s_r_ff_1 (
    .S(decoder_1_out8), .R(decoder_1_out9), .clk(Clk), .Q(s_r_ff_1_q));  // open: reset, Qn, preset
  Register register_1 (.D(ReadIn), .en(s_r_ff_3_q), .clk(Button), .Q(register_1_q));  // open: clr
  S_R_Flip_Flop #(.trigger("falling")) s_r_ff_2 (
    .S(decoder_1_out14), .R(decoder_1_out15), .clk(Clk), .Q(s_r_ff_2_q));  // open: reset, Qn, preset
  Register register_2 (.D(GPInput), .en(1'b1), .clk(Clk), .Q(register_2_q));  // open: clr
  assign DATA = s_r_ff_1_q ? register_1_q : 8'bz;  // Controlled_Buffer controlled_buffer_1
  assign DATA = s_r_ff_2_q ? register_2_q : 8'bz;  // Controlled_Buffer controlled_buffer_2
  S_R_Flip_Flop #(.trigger("falling")) s_r_ff_3 (
    .S(decoder_1_out7), .R(1'b0), .clk(Clk), .Q(s_r_ff_3_q), .reset(Button));  // open: Qn, preset
  buf or_1 (HALT, s_r_ff_3_q);  // OR_Gate
endmodule

module Stack (
  input  Misc,
  input  [7:0] ROM,
  input  [7:0] Data,
  input  Clock,
  output [7:0] ReadStack,
  output ResetCOUT
);

  wire and_1_out, and_2_out, decoder_1_out10, decoder_1_out11, decoder_1_out12, decoder_1_out13, s_r_ff_1_q;
  wire [7:0] shift_register_1_p4;

  Decoder #(.select(4)) decoder_1 (
    .out10(decoder_1_out10), .out11(decoder_1_out11), .out12(decoder_1_out12), .out13(decoder_1_out13),
    .sel(ROM[7:4]), .en(Misc));  // open: out0, out1, out2, out3, out4, out5, out6, out7, out8, out9, out14, out15
  // Shift_Register #(.width(8), .length(4), .parallel("false")) shift_register_1: pin names not known; wires that end beside it: decoder_1_out12, Clock, Data, shift_register_1_p4
  S_R_Flip_Flop s_r_ff_1 (
    .S(decoder_1_out10), .R(decoder_1_out11), .clk(Clock), .Q(s_r_ff_1_q));  // open: reset, Qn, preset
  and and_1 (and_1_out, decoder_1_out13, Clock);
  assign ReadStack = s_r_ff_1_q ? shift_register_1_p4 : 8'bz;  // Controlled_Buffer controlled_buffer_1
  S_R_Flip_Flop #(.trigger("falling")) s_r_ff_2 (
    .S(and_1_out), .R(and_2_out), .clk(Clock), .Q(ResetCOUT));  // open: reset, Qn, preset
  and and_2 (and_2_out, ~and_1_out, Clock);  // AND_Gate
endmodule
