// Logisim project COMPUTER_ZERO.circ as structural Verilog: 2 circuits, main circuit main
module main (
);

  wire AccumulatorIsZero, AccumulatorOut, Add, and_1_out, and_2_out, and_3_out, Carry, CarryIn, Clk,
       comparator_1_eq, decoder_1_out3, decoder_1_out4, decoder_1_out5, decoder_1_out7, decoder_1_out8,
       decoder_1_out9, decoder_1_out10, decoder_1_out14, decoder_1_out15, ldPC, Load, RstCrry, Save, SetA,
       t_ff_1_q, t_ff_2_q, ToggleSub, WriteOutput;
  wire [7:0] counter_1_q, Data, register_1_q;
  wire [11:0] rom_1_data;

  Counter #(.ongoal("stay")) counter_1 (
    .load(ldPC), .up(1'b1), .count(1'b1), .clk(Clk), .D(rom_1_data[7:0]), .Q(counter_1_q));  // open: clr, carry
  Clock clock_1 (.out(Clk));
  ROM #(.dataWidth(12)) rom_1 (.addr(counter_1_q), .data(rom_1_data));
  T_Flip_Flop t_ff_1 (.T(ToggleSub), .clk(Clk), .Q(t_ff_1_q));  // open: Qn, reset, preset
  Decoder #(.select(4), .enable("false")) decoder_1 (
    .out1(Save), .out2(WriteOutput), .out3(decoder_1_out3), .out4(decoder_1_out4), .out5(decoder_1_out5),
    .out6(Add), .out7(decoder_1_out7), .out8(decoder_1_out8), .out9(decoder_1_out9), .out10(decoder_1_out10),
    .out11(SetA), .out12(ToggleSub), .out13(RstCrry), .out14(decoder_1_out14), .out15(decoder_1_out15),
    .sel(rom_1_data[11:8]));  // open: out0
  T_Flip_Flop t_ff_2 (.T(decoder_1_out14), .clk(Clk), .Q(t_ff_2_q));  // open: Qn, reset, preset
  assign Data = t_ff_2_q ? rom_1_data[7:0] : 8'bz;  // Controlled_Buffer controlled_buffer_1
  Hex_Digit_Display hex_digit_display_1 (.value(Data[7:4]));  // open: dp
  T_Flip_Flop t_ff_3 (.T(decoder_1_out9), .clk(Clk), .Q(Load));  // open: Qn, reset, preset
  LED led_1 (.in(AccumulatorIsZero));
  Hex_Digit_Display hex_digit_display_2 (.value(Data[3:0]));  // open: dp
  ALU alu_1 (
    .Sub(t_ff_1_q), .CarryIn(CarryIn), .Ain(Data), .SetA(SetA), .AccumulatorOut(AccumulatorOut), .Add(Add),
    .ResetCarryOut(RstCrry), .Clock(Clk), .Accumulator(Data), .AccumulatorIsZero(AccumulatorIsZero),
    .CarryOut(Carry));  // open: ResetAcum
  Register register_1 (.D(rom_1_data[7:0]), .en(decoder_1_out15), .clk(Clk), .Q(register_1_q));  // open: clr
  LED led_2 (.in(Carry));
  and and_1 (and_1_out, decoder_1_out4, AccumulatorIsZero);
  and and_2 (and_2_out, decoder_1_out5, Carry);
  T_Flip_Flop t_ff_4 (.T(decoder_1_out8), .clk(Clk), .Q(CarryIn));  // open: Qn, reset, preset
  T_Flip_Flop t_ff_5 (.T(decoder_1_out7), .clk(Clk), .Q(AccumulatorOut));  // open: Qn, reset, preset
  and and_3 (and_3_out, decoder_1_out10, comparator_1_eq);
  RAM ram_1 (.addr(rom_1_data[7:0]), .we(Save), .oe(Load), .clk(Clk), .data(Data));
  Register register_2 (.D(Data), .en(WriteOutput), .clk(Clk));  // open: Q, clr
  or or_1 (ldPC, decoder_1_out3, and_1_out, and_2_out, and_3_out);
  Comparator #(.mode("unsigned")) comparator_1 (.a(Data), .b(register_1_q), .eq(comparator_1_eq));  // open: gt, lt
  // BCD_to_7_Segment_decoder bcd_to_7_segment_decoder_1: pin names not known
  _7_Segment_Display u_7_segment_display_1 ();  // open: g, f, a, b, e, d, c, dp
  // Binairy_to_BCD_converter #(.binvalue(8)) binairy_to_bcd_converter_1: pin names not known
  // BCD_to_7_Segment_decoder bcd_to_7_segment_decoder_2: pin names not known
  _7_Segment_Display u_7_segment_display_2 ();  // open: g, f, a, b, e, d, c, dp
  _7_Segment_Display u_7_segment_display_3 ();  // open: g, f, a, b, e, d, c, dp
  // BCD_to_7_Segment_decoder bcd_to_7_segment_decoder_3: pin names not known

  // Notes on the sheet:
  //   contents of rom_1 (hex, n*v repeats v):
  //   e00 b01 f0a e00 700 a09 600 200 305 b00 c00 600 200 30d
endmodule

module ALU (
  input  Sub,
  input  CarryIn,
  input  [7:0] Ain,
  input  SetA,
  input  AccumulatorOut,
  input  Add,
  input  ResetAcum,
  input  ResetCarryOut,
  input  Clock,
  output [7:0] Accumulator,
  output AccumulatorIsZero,
  output CarryOut
);

  wire adder_1_cout, or_1_out;
  wire [7:0] Accum_q, adder_1_out, multiplexer_1_out, negator_1_out, register_1_q;

  Register register_1 (.D(Ain), .en(SetA), .clk(Clock), .Q(register_1_q));  // open: clr
  Negator negator_1 (.in(register_1_q), .out(negator_1_out));
  Multiplexer #(.width(8), .enable("false")) multiplexer_1 (
    .in0(register_1_q), .in1(negator_1_out), .out(multiplexer_1_out), .sel(Sub));
  Adder adder_1 (.a(multiplexer_1_out), .b(Accum_q), .out(adder_1_out), .cin(CarryIn), .cout(adder_1_cout));
  Register Accum (.D(adder_1_out), .en(Add), .clk(Clock), .Q(Accum_q), .clr(ResetAcum));
  S_R_Flip_Flop s_r_ff_1 (.S(adder_1_cout), .R(ResetCarryOut), .clk(Clock), .Q(CarryOut));  // open: reset, Qn, preset
  assign Accumulator = AccumulatorOut ? Accum_q : 8'bz;  // Controlled_Buffer controlled_buffer_1
  or or_1 (or_1_out, Accum_q[0], Accum_q[1], Accum_q[2], Accum_q[3], Accum_q[4], Accum_q[5], Accum_q[6], Accum_q[7]);
  not not_1 (AccumulatorIsZero, or_1_out);
endmodule
